// Logisim project 25CSB1A77_RahulKumarChaurasiya_COA.circ as structural Verilog: 4 circuits, main circuit main
module main (
  input  Outside,
  input  Inside,
  input  EMERGENCY_ACTIVE,
  input  OVERLOAD,
  output EMERGENCY
);

  wire Call0_FF2_q, Call0_FF_q, Call1_FF2_q, Call1_FF_q, Call2_FF2_q, Call2_FF_q, CALL_Ground_out,
       CALL_to_1st_out, CALL_to_2nd_out, Clock_out, decoder_1_out0, decoder_1_out1, decoder_2_out0,
       decoder_2_out1, display_1_a, display_1_b, display_1_c, display_1_d, display_1_dot, display_1_e,
       display_1_f, display_1_g, elevator_1_busy, elevator_1_door, elevator_1_down, elevator_1_floor0,
       elevator_1_floor1, elevator_1_floor2, elevator_1_up, Floor_0_q, Floor_1_q, Floor_2_q,
       floor_buttons_1_call0_trig, floor_buttons_1_call1_trig, floor_buttons_1_call2_trig,
       floor_buttons_1_go0_trig, floor_buttons_1_go1_trig, floor_buttons_1_go2_trig, Go0_FF2_q, Go0_FF_q,
       Go1_FF2_q, Go1_FF_q, Go2_FF2_q, Go2_FF_q, GO_1st_out, Go_2nd_out, GO_Ground_out, not_1_out, or_1_out,
       or_2_out, or_3_out, or_4_out, or_5_out, or_6_out;

  or or_1 (or_1_out, Call0_FF2_q, Call0_FF_q);
  or or_2 (or_2_out, Call2_FF2_q, Call2_FF_q);
  or or_3 (or_3_out, Go1_FF2_q, Go1_FF_q);
  Clock Clock (.out(Clock_out));
  D_Flip_Flop Floor_0 (.clk(Clock_out), .D(elevator_1_floor0), .Q(Floor_0_q));  // open: Qn, preset, en, reset
  D_Flip_Flop Floor_1 (.clk(Clock_out), .D(elevator_1_floor1), .Q(Floor_1_q));  // open: Qn, preset, en, reset
  D_Flip_Flop Floor_2 (.clk(Clock_out), .D(elevator_1_floor2), .Q(Floor_2_q));  // open: Qn, preset, en, reset
  D_Flip_Flop Call0_FF2 (.clk(Clock_out), .D(Call0_FF_q), .Q(Call0_FF2_q));  // open: Qn, preset, en, reset
  D_Flip_Flop Call0_FF (
    .clk(Clock_out), .D(floor_buttons_1_call0_trig), .Q(Call0_FF_q));  // open: Qn, preset, en, reset
  D_Flip_Flop Call2_FF2 (.clk(Clock_out), .D(Call2_FF_q), .Q(Call2_FF2_q));  // open: Qn, preset, en, reset
  D_Flip_Flop Call2_FF (
    .clk(Clock_out), .D(floor_buttons_1_call2_trig), .Q(Call2_FF_q));  // open: Qn, preset, en, reset
  D_Flip_Flop Go1_FF2 (.clk(Clock_out), .D(Go1_FF_q), .Q(Go1_FF2_q));  // open: Qn, preset, en, reset
  D_Flip_Flop Go1_FF (.clk(Clock_out), .D(floor_buttons_1_go1_trig), .Q(Go1_FF_q));  // open: Qn, preset, en, reset
  D_Flip_Flop Call1_FF2 (.clk(Clock_out), .D(Call1_FF_q), .Q(Call1_FF2_q));  // open: Qn, preset, en, reset
  or or_4 (or_4_out, Call1_FF2_q, Call1_FF_q);
  D_Flip_Flop Call1_FF (
    .clk(Clock_out), .D(floor_buttons_1_call1_trig), .Q(Call1_FF_q));  // open: Qn, preset, en, reset
  D_Flip_Flop Go0_FF2 (.clk(Clock_out), .D(Go0_FF_q), .Q(Go0_FF2_q));  // open: Qn, preset, en, reset
  or or_5 (or_5_out, Go0_FF2_q, Go0_FF_q);
  D_Flip_Flop Go0_FF (.clk(Clock_out), .D(floor_buttons_1_go0_trig), .Q(Go0_FF_q));  // open: Qn, preset, en, reset
  D_Flip_Flop Go2_FF2 (.clk(Clock_out), .D(Go2_FF_q), .Q(Go2_FF2_q));  // open: Qn, preset, en, reset
  or or_6 (or_6_out, Go2_FF2_q, Go2_FF2_q, Go2_FF_q, Go2_FF_q, Go2_FF_q);
  D_Flip_Flop Go2_FF (.clk(Clock_out), .D(floor_buttons_1_go2_trig), .Q(Go2_FF_q));  // open: Qn, preset, en, reset
  LED ACTIVE (.in(OVERLOAD));
  elevator elevator_1 (
    .floor0_trig(Floor_0_q), .floor1_trig(Floor_1_q), .floor2_trig(Floor_2_q), .call0_btn(or_1_out),
    .call1_btn(or_4_out), .call2_btn(or_2_out), .go0_btn(or_5_out), .go1_btn(or_3_out), .go2_btn(or_6_out),
    .emergency(EMERGENCY_ACTIVE), .floor0(elevator_1_floor0), .floor1(elevator_1_floor1),
    .floor2(elevator_1_floor2), .busy(elevator_1_busy), .door(elevator_1_door), .up(elevator_1_up),
    .down(elevator_1_down));
  Decoder #(.enable("false")) decoder_1 (.out0(decoder_1_out0), .out1(decoder_1_out1), .sel(elevator_1_door));
  LED Floor_0_2 (.in(elevator_1_floor0));
  not not_1 (not_1_out, elevator_1_busy);
  Decoder #(.enable("false")) decoder_2 (.out0(decoder_2_out0), .out1(decoder_2_out1), .sel(elevator_1_busy));
  LED Floor_1_2 (.in(elevator_1_floor1));
  display display_1 (
    .floor0(elevator_1_floor0), .floor1(elevator_1_floor1), .floor2(elevator_1_floor2), .a(display_1_a),
    .b(display_1_b), .c(display_1_c), .d(display_1_d), .e(display_1_e), .f(display_1_f), .g(display_1_g),
    .dot(display_1_dot));
  LED Floor_2_2 (.in(elevator_1_floor2));
  _7_Segment_Display u_7_segment_display_1 (
    .g(display_1_g), .f(display_1_f), .a(display_1_a), .b(display_1_b), .e(display_1_e), .d(display_1_d),
    .c(display_1_c), .dp(display_1_dot));
  LED Door_Closed (.in(decoder_1_out1));
  LED Door_Open (.in(decoder_1_out0));
  LED Up (.in(elevator_1_up));
  LED Down (.in(elevator_1_down));
  LED Ready (.in(not_1_out));
  LED led_1 (.in(EMERGENCY_ACTIVE));
  Button CALL_to_2nd (.out(CALL_to_2nd_out));
  Button CALL_to_1st (.out(CALL_to_1st_out));
  Button CALL_Ground (.out(CALL_Ground_out));
  LED Busy (.in(decoder_2_out1));
  LED Usable (.in(decoder_2_out0));
  Button Go_2nd (.out(Go_2nd_out));
  Button GO_1st (.out(GO_1st_out));
  Button GO_Ground (.out(GO_Ground_out));
  floor_buttons floor_buttons_1 (
    .go2(Go_2nd_out), .go1(GO_1st_out), .go0(GO_Ground_out), .call2(CALL_to_2nd_out),
    .call1(CALL_to_1st_out), .call0(CALL_Ground_out), .go2_trig(floor_buttons_1_go2_trig),
    .go1_trig(floor_buttons_1_go1_trig), .go0_trig(floor_buttons_1_go0_trig),
    .call2_trig(floor_buttons_1_call2_trig), .call1_trig(floor_buttons_1_call1_trig),
    .call0_trig(floor_buttons_1_call0_trig));

  assign EMERGENCY = EMERGENCY_ACTIVE;

  // Notes on the sheet:
  //   Flip-Flop Clock / Triggering
  //   Floor Display
endmodule

module display (
  input  floor0,
  input  floor1,
  input  floor2,
  output a,
  output b,
  output c,
  output d,
  output e,
  output f,
  output g,
  output dot
);

  wire and_1_out, and_2_out, and_3_out, and_4_out, and_5_out, and_6_out, and_7_out, and_8_out, and_9_out,
       and_10_out, and_11_out, not_1_out, not_2_out, not_3_out, not_4_out, not_5_out, not_6_out, not_7_out,
       not_8_out, not_9_out, not_10_out, not_11_out, not_12_out, not_13_out, not_14_out, not_15_out,
       not_16_out, not_17_out, not_18_out, not_19_out, not_20_out, not_21_out, not_22_out, not_23_out,
       not_24_out, not_25_out, not_26_out;

  not not_1 (not_1_out, floor0);
  not not_2 (not_2_out, floor1);
  not not_3 (not_3_out, floor1);
  not not_4 (not_4_out, floor2);
  not not_5 (not_5_out, floor0);
  not not_6 (not_6_out, floor1);
  not not_7 (not_7_out, floor0);
  not not_8 (not_8_out, floor2);
  not not_9 (not_9_out, floor1);
  not not_10 (not_10_out, floor2);
  not not_11 (not_11_out, floor0);
  not not_12 (not_12_out, floor2);
  not not_13 (not_13_out, floor1);
  not not_14 (not_14_out, floor2);
  not not_15 (not_15_out, floor0);
  not not_16 (not_16_out, floor1);
  not not_17 (not_17_out, floor1);
  not not_18 (not_18_out, floor2);
  not not_19 (not_19_out, floor0);
  not not_20 (not_20_out, floor1);
  not not_21 (not_21_out, floor1);
  not not_22 (not_22_out, floor2);
  not not_23 (not_23_out, floor1);
  not not_24 (not_24_out, floor2);
  not not_25 (not_25_out, floor0);
  not not_26 (not_26_out, floor1);
  and and_1 (and_1_out, not_1_out, not_2_out, floor2);
  and and_2 (and_2_out, floor0, not_3_out, not_4_out);
  and and_3 (and_3_out, not_5_out, not_6_out, floor2);
  and and_4 (and_4_out, not_7_out, floor1, not_8_out);
  and and_5 (and_5_out, floor0, not_9_out, not_10_out);
  and and_6 (and_6_out, not_11_out, floor1, not_12_out);
  and and_7 (and_7_out, floor0, not_13_out, not_14_out);
  and and_8 (and_8_out, not_15_out, not_16_out, floor2);
  and and_9 (and_9_out, floor0, not_17_out, not_18_out);
  and and_10 (and_10_out, not_19_out, not_20_out, floor2);
  and and_11 (and_11_out, floor0, not_21_out, not_22_out);
  and and_12 (f, floor0, not_23_out, not_24_out);
  and and_13 (g, not_25_out, not_26_out, floor2);
  or or_1 (a, and_1_out, and_2_out);
  or or_2 (b, and_3_out, and_4_out, and_5_out);
  or or_3 (c, and_6_out, and_7_out);
  or or_4 (d, and_8_out, and_9_out);
  or or_5 (e, and_10_out, and_11_out);

  assign dot = 1'b1;
endmodule

module elevator (
  input  floor0_trig,
  input  floor1_trig,
  input  floor2_trig,
  input  call0_btn,
  input  call1_btn,
  input  call2_btn,
  input  go0_btn,
  input  go1_btn,
  input  go2_btn,
  input  emergency,
  output floor0,
  output floor1,
  output floor2,
  output busy,
  output door,
  output up,
  output down
);

  wire and_1_out, and_2_out, and_3_out, and_4_out, and_5_out, and_6_out, and_7_out, and_8_out, and_9_out,
       and_10_out, and_11_out, and_12_out, and_13_out, and_14_out, and_15_out, and_16_out, and_17_out,
       and_18_out, and_19_out, and_20_out, and_21_out, and_22_out, and_23_out, and_24_out, and_25_out,
       and_26_out, and_27_out, and_28_out, and_29_out, and_30_out, and_31_out, and_32_out, and_33_out,
       and_34_out, and_35_out, and_36_out, and_37_out, and_38_out, and_39_out, and_40_out, and_41_out,
       and_42_out, and_43_out, not_1_out, not_2_out, not_3_out, not_4_out, not_5_out, not_6_out, not_7_out,
       not_8_out, not_9_out, not_10_out, not_11_out, not_12_out, not_13_out, not_14_out, not_15_out,
       not_16_out, not_17_out, not_18_out, not_19_out, not_20_out, not_21_out, not_22_out, not_23_out,
       not_24_out, not_25_out, not_26_out, not_27_out, not_28_out, not_29_out, not_30_out, not_31_out,
       not_32_out, not_33_out, not_34_out, not_35_out, not_36_out, not_37_out, not_38_out, not_39_out,
       not_40_out, not_41_out, not_42_out, not_43_out, or_6_out, or_7_out;

  not not_1 (not_1_out, floor1_trig);
  not not_2 (not_2_out, floor2_trig);
  not not_3 (not_3_out, call1_btn);
  not not_4 (not_4_out, call2_btn);
  not not_5 (not_5_out, go1_btn);
  not not_6 (not_6_out, go2_btn);
  not not_7 (not_7_out, floor2_trig);
  not not_8 (not_8_out, floor2_trig);
  not not_9 (not_9_out, call0_btn);
  not not_10 (not_10_out, call2_btn);
  not not_11 (not_11_out, go0_btn);
  not not_12 (not_12_out, go2_btn);
  not not_13 (not_13_out, floor0_trig);
  not not_14 (not_14_out, floor0_trig);
  not not_15 (not_15_out, call0_btn);
  not not_16 (not_16_out, call1_btn);
  not not_17 (not_17_out, go0_btn);
  not not_18 (not_18_out, go1_btn);
  not not_19 (not_19_out, floor2_trig);
  not not_20 (not_20_out, floor1_trig);
  not not_21 (not_21_out, floor0_trig);
  not not_22 (not_22_out, floor2_trig);
  not not_23 (not_23_out, floor1_trig);
  not not_24 (not_24_out, floor2_trig);
  not not_25 (not_25_out, floor1_trig);
  not not_26 (not_26_out, floor1_trig);
  not not_27 (not_27_out, floor2_trig);
  not not_28 (not_28_out, floor1_trig);
  not not_29 (not_29_out, floor2_trig);
  not not_30 (not_30_out, floor0_trig);
  not not_31 (not_31_out, floor2_trig);
  not not_32 (not_32_out, call0_btn);
  not not_33 (not_33_out, call1_btn);
  not not_34 (not_34_out, go0_btn);
  not not_35 (not_35_out, go1_btn);
  not not_36 (not_36_out, floor1_trig);
  not not_37 (not_37_out, floor2_trig);
  not not_38 (not_38_out, floor1_trig);
  not not_39 (not_39_out, floor2_trig);
  not not_40 (not_40_out, floor0_trig);
  not not_41 (not_41_out, call2_btn);
  not not_42 (not_42_out, go2_btn);
  and and_1 (and_1_out, not_1_out, not_2_out, not_3_out, not_4_out, not_5_out, not_6_out);
  and and_2 (and_2_out, not_7_out, go0_btn);
  and and_3 (and_3_out, not_8_out, call0_btn);
  and and_4 (and_4_out, floor2_trig, go0_btn);
  and and_5 (and_5_out, floor2_trig, call0_btn);
  and and_6 (and_6_out, floor1_trig, not_9_out, not_10_out, not_11_out, not_12_out);
  and and_7 (and_7_out, floor0_trig, go2_btn);
  and and_8 (and_8_out, floor0_trig, call2_btn);
  and and_9 (and_9_out, not_13_out, go2_btn);
  and and_10 (and_10_out, not_14_out, call2_btn);
  and and_11 (and_11_out, floor2_trig, not_15_out, not_16_out, not_17_out, not_18_out);
  and and_12 (and_12_out, not_19_out, go2_btn);
  and and_13 (and_13_out, not_20_out, go1_btn);
  and and_14 (and_14_out, not_21_out, go0_btn);
  and and_15 (and_15_out, not_22_out, call2_btn);
  and and_16 (and_16_out, not_23_out, call1_btn);
  and and_17 (and_17_out, floor2_trig, call0_btn);
  and and_18 (and_18_out, floor1_trig, call0_btn);
  and and_19 (and_19_out, not_24_out, go2_btn);
  and and_20 (and_20_out, not_25_out, go1_btn);
  and and_21 (and_21_out, not_26_out, call1_btn);
  and and_22 (and_22_out, floor2_trig, go0_btn);
  and and_23 (and_23_out, floor2_trig, call0_btn);
  and and_24 (and_24_out, floor1_trig, go0_btn);
  and and_25 (and_25_out, floor1_trig, call2_btn);
  and and_26 (and_26_out, floor1_trig, call0_btn);
  and and_27 (and_27_out, floor0_trig, call2_btn);
  and and_28 (and_28_out, not_27_out, go2_btn);
  and and_29 (and_29_out, not_28_out, not_29_out, go1_btn);
  and and_30 (and_30_out, not_30_out, not_31_out, not_32_out, not_33_out, call2_btn, not_34_out, not_35_out);
  and and_31 (and_31_out, not_36_out, not_37_out, call2_btn);
  and and_32 (and_32_out, not_38_out, not_39_out, call1_btn);
  and and_33 (and_33_out, floor2_trig, go1_btn);
  and and_34 (and_34_out, not_40_out, floor2_trig, not_41_out, go0_btn, not_42_out);
  and and_35 (and_35_out, floor2_trig, call1_btn);
  and and_36 (and_36_out, floor2_trig, call0_btn);
  and and_37 (and_37_out, floor1_trig, go0_btn);
  and and_38 (and_38_out, floor1_trig, call2_btn, go2_btn);
  and and_39 (and_39_out, floor1_trig, call2_btn, go1_btn);
  and and_40 (and_40_out, floor1_trig, call1_btn, call2_btn);
  and and_41 (and_41_out, floor1_trig, call0_btn);
  and and_42 (and_42_out, floor1_trig, floor2_trig, call2_btn);
  and and_43 (and_43_out, floor0_trig, floor1_trig, call2_btn);
  or or_1 (floor0, and_1_out, and_2_out, and_3_out);
  or or_2 (floor1, go1_btn, call1_btn, and_4_out, and_5_out, and_6_out, and_7_out, and_8_out);
  or or_3 (floor2, and_9_out, and_10_out, and_11_out);
  or or_4 (busy, and_12_out, and_13_out, and_14_out, and_15_out, and_16_out, and_17_out, and_18_out);
  or or_5 (door, and_19_out, and_20_out, and_21_out, and_22_out, and_23_out, and_24_out, and_25_out, and_26_out, and_27_out);
  or or_6 (or_6_out, and_28_out, and_29_out, and_30_out, and_31_out, and_32_out);
  or or_7 (or_7_out, and_33_out, and_34_out, and_35_out, and_36_out, and_37_out, and_38_out, and_39_out, and_40_out, and_41_out, and_42_out, and_43_out);
  not not_43 (not_43_out, emergency);
  and and_44 (up, or_6_out, not_43_out);
  and and_45 (down, not_43_out, or_7_out);
endmodule

module floor_buttons (
  input  go2,
  input  go1,
  input  go0,
  input  call2,
  input  call1,
  input  call0,
  output go2_trig,
  output go1_trig,
  output go0_trig,
  output call2_trig,
  output call1_trig,
  output call0_trig
);

  wire clock_1_out;

  Clock clock_1 (.out(clock_1_out));
  D_Flip_Flop Go2_FF (.Q(go2_trig), .preset(go2), .reset(clock_1_out));  // open: clk, D, Qn, en
  D_Flip_Flop Go1_FF (.Q(go1_trig), .preset(go1), .reset(clock_1_out));  // open: clk, D, Qn, en
  D_Flip_Flop Go0_FF (.Q(go0_trig), .preset(go0), .reset(clock_1_out));  // open: clk, D, Qn, en
  D_Flip_Flop Call2_FF (.Q(call2_trig), .preset(call2), .reset(clock_1_out));  // open: clk, D, Qn, en
  D_Flip_Flop Call1_FF (.Q(call1_trig), .preset(call1), .reset(clock_1_out));  // open: clk, D, Qn, en
  D_Flip_Flop Call0_FF (.Q(call0_trig), .preset(call0), .reset(clock_1_out));  // open: clk, D, Qn, en
endmodule
